# Fritzing sketch Pong3D (saved by Fritzing 0.9.2b)
circuit board: 8.46667cm x 5.64444cm
breadboards: 1

parts:
  Arduino = Arduino Uno (Rev3)
  R1 = Rotary Potentiometer (Small) [maximum_resistance=100kΩ package=THT]
  R2 = Rotary Potentiometer (Small) [maximum_resistance=100kΩ package=THT]

nets:
  N1: Arduino.A0, R1.wiper
  N2: Arduino.A1, R2.wiper
  N3: Arduino.GND, R1.leg1, R2.leg1
  N4: Arduino.5V, R1.leg2, R2.leg2
